# Fritzing sketch circuit-board_2_ir (saved by Fritzing 0.9.0b)
perfboards: 1

parts:
  IR2 = TSOP312.., 314.. [part_number=TSOP4838 package=THT]  # not connected
  Q2 = NPN-Transistor [part_number=BC547c package="TO92 [THT]"]
  IR-Emitter1 = LED - 5mm [color="Infrared (940nm)" package="5 mm [THT]"]
  R2 = Resistor [tolerance=±5% resistance=100 package=THT]
  R3 = Resistor [tolerance=±5% resistance=1k package=THT]
  Q3 = NPN-Transistor [part_number=BC547c package="TO92 [THT]"]
  IR-Emitter2 = LED - 5mm [color="Infrared (940nm)" package="5 mm [THT]"]
  R4 = Resistor [tolerance=±5% resistance=1k package=THT]
  R5 = Resistor [tolerance=±5% resistance=100 package=THT]  # not connected

nets:
  N1: Q2.E, Q3.E
  N2: Q2.B, R3.Pin_1
  N3: Q2.C, IR-Emitter1.cathode
  N4: IR-Emitter1.anode, R2.Pin_1
  N5: Q3.B, R4.Pin_1
  N6: Q3.C, IR-Emitter2.cathode
